# Fritzing sketch Radio-raspberrypi (saved by Fritzing 0.9.10b)

parts:
  Mod1 = Raspberry Pi 4B
  Part1 = NRF24L01+ Breakout Board

nets:
  3V3: Mod1.3V3, Part1.VCC
  GND: Mod1.GND, Part1.GND
  N1: Mod1.GPIO22, Part1.CE
  N2: Mod1.GPIO10, Part1.MOSI
  N3: Mod1.GPIO9, Part1.MISO
  N4: Mod1.GPIO11, Part1.SCK
  N5: Mod1.GPIO8, Part1.CS
